// Logisim project Processador.circ as structural Verilog: 5 circuits, main circuit Processador
module Processador (
  input  in_1,
  input  En
);

  wire and_1_out, Ck, ula_1_zero, uni_cont_1_beq, uni_cont_1_jump, uni_cont_1_memread, uni_cont_1_memtoreg,
       uni_cont_1_memwrite, uni_cont_1_regwrite, uni_cont_1_ula_src;
  wire [1:0] rom_1_data_2, rom_1_data_3, uni_cont_1_ula_op;
  wire [7:0] adder_1_out, adder_2_out, banco_de_regs_1_s1, banco_de_regs_1_s2, multiplexer_1_out,
       multiplexer_2_out, multiplexer_3_out, multiplexer_4_out, PC_q, ram_1_data, rom_1_data, shifter_1_out,
       shifter_2_out, ula_1_out;

  Clock clock_1 (.out(Ck));
  Register PC (.D(multiplexer_3_out), .en(Ck), .Q(PC_q), .clr(in_1));  // open: clk
  Adder adder_1 (.a(PC_q), .b(8'h4), .out(adder_1_out));  // open: cin, cout
  ROM rom_1 (
    .addr(PC_q),
    .data({rom_1_data[7:5], rom_1_data_3[0], rom_1_data_3[1], rom_1_data_2[0], rom_1_data_2[1], rom_1_data[0]}));  // open: sel
  Shifter shifter_1 (
    .in({1'b0, adder_1_out[7:6], rom_1_data_3, rom_1_data_2, rom_1_data[0]}), .\dist (3'b010),
    .out(shifter_1_out));
  Uni_Cont uni_cont_1 (
    .RegWrite(uni_cont_1_regwrite), .Beq(uni_cont_1_beq), .MemWrite(uni_cont_1_memwrite),
    .MemRead(uni_cont_1_memread), .MemToReg(uni_cont_1_memtoreg), .Jump(uni_cont_1_jump),
    .ULA_Src(uni_cont_1_ula_src), .ULA_OP(uni_cont_1_ula_op), .En(En), .Seletor(rom_1_data[7:5]));
  Banco_de_Regs banco_de_regs_1 (
    .RegWrite(Ck), .Enable(uni_cont_1_regwrite), .In_D(multiplexer_4_out), .Sel_Dado(rom_1_data_2),
    .Clear(in_1), .R1(rom_1_data_3), .R2(rom_1_data_2), .S1(banco_de_regs_1_s1), .S2(banco_de_regs_1_s2));
  Multiplexer #(.width(8), .enable("false")) multiplexer_1 (
    .in0(banco_de_regs_1_s2), .in1({{7{1'b0}}, rom_1_data[0]}), .out(multiplexer_1_out),
    .sel(uni_cont_1_ula_src));
  Multiplexer #(.width(8), .enable("false")) multiplexer_2 (
    .in0(shifter_1_out), .in1(adder_1_out), .out(multiplexer_2_out), .sel(uni_cont_1_jump));
  ULA ula_1 (
    .InA(banco_de_regs_1_s1), .InB(multiplexer_1_out), .ULA_OP(uni_cont_1_ula_op), .Out(ula_1_out),
    .Zero(ula_1_zero));
  Shifter shifter_2 (.in({{7{1'b0}}, rom_1_data[0]}), .\dist (3'b010), .out(shifter_2_out));
  and and_1 (and_1_out, uni_cont_1_beq, ula_1_zero);
  Adder adder_2 (.a(multiplexer_2_out), .b(shifter_2_out), .out(adder_2_out));  // open: cin, cout
  Multiplexer #(.width(8), .enable("false")) multiplexer_3 (
    .in0(multiplexer_2_out), .in1(adder_2_out), .out(multiplexer_3_out), .sel(and_1_out));
  RAM #(.bus("separate")) ram_1 (
    .addr(ula_1_out), .din(banco_de_regs_1_s2), .data(ram_1_data), .str(uni_cont_1_memwrite), .clk(Ck),
    .ld(uni_cont_1_memread));  // open: sel, clr
  Multiplexer #(.width(8), .enable("false")) multiplexer_4 (
    .in0(ula_1_out), .in1(ram_1_data), .out(multiplexer_4_out), .sel(uni_cont_1_memtoreg));

  // Other names for the same wires on the sheet: Cl = in_1
endmodule

module Regs_de_8_bits (
  input  Clear,
  input  Clock,
  input  [7:0] In,
  output [7:0] Out
);

  D_Flip_Flop d_ff_1 (.clk(Clock), .D(In[7]), .Q(Out[7]), .reset(Clear));  // open: Qn, preset, en
  D_Flip_Flop d_ff_2 (.clk(Clock), .D(In[6]), .Q(Out[6]), .reset(Clear));  // open: Qn, preset, en
  D_Flip_Flop d_ff_3 (.clk(Clock), .D(In[5]), .Q(Out[5]), .reset(Clear));  // open: Qn, preset, en
  D_Flip_Flop d_ff_4 (.clk(Clock), .D(In[4]), .Q(Out[4]), .reset(Clear));  // open: Qn, preset, en
  D_Flip_Flop d_ff_5 (.clk(Clock), .D(In[3]), .Q(Out[3]), .reset(Clear));  // open: Qn, preset, en
  D_Flip_Flop d_ff_6 (.clk(Clock), .D(In[2]), .Q(Out[2]), .reset(Clear));  // open: Qn, preset, en
  D_Flip_Flop d_ff_7 (.clk(Clock), .D(In[1]), .Q(Out[1]), .reset(Clear));  // open: Qn, preset, en
  D_Flip_Flop d_ff_8 (.clk(Clock), .D(In[0]), .Q(Out[0]), .reset(Clear));  // open: Qn, preset, en
endmodule

// Banco de Registradores
module Banco_de_Regs (
  input  RegWrite,
  input  Enable,
  input  [1:0] Sel_Dado,
  input  [1:0] R1,
  input  [7:0] In_D,
  input  Clear,
  input  [1:0] R2,
  output [7:0] S1,
  output [7:0] S2
);

  wire demultiplexer_1_out0, demultiplexer_1_out1, demultiplexer_1_out2, demultiplexer_1_out3;
  wire [7:0] regs_de_8_bits_1_out, regs_de_8_bits_2_out, regs_de_8_bits_3_out, regs_de_8_bits_4_out;

  Demultiplexer #(.select(2)) demultiplexer_1 (
    .out0(demultiplexer_1_out0), .out1(demultiplexer_1_out1), .out2(demultiplexer_1_out2),
    .out3(demultiplexer_1_out3), .in(RegWrite), .sel(Sel_Dado), .en(Enable));
  Regs_de_8_bits regs_de_8_bits_1 (.Clear(Clear), .Clock(demultiplexer_1_out0), .In(In_D), .Out(regs_de_8_bits_1_out));
  Regs_de_8_bits regs_de_8_bits_2 (.Clear(Clear), .Clock(demultiplexer_1_out1), .In(In_D), .Out(regs_de_8_bits_2_out));
  Regs_de_8_bits regs_de_8_bits_3 (.Clear(Clear), .Clock(demultiplexer_1_out2), .In(In_D), .Out(regs_de_8_bits_3_out));
  Regs_de_8_bits regs_de_8_bits_4 (.Clear(Clear), .Clock(demultiplexer_1_out3), .In(In_D), .Out(regs_de_8_bits_4_out));
  Multiplexer #(.select(2), .width(8), .enable("false")) multiplexer_1 (
    .in0(regs_de_8_bits_1_out), .in1(regs_de_8_bits_2_out), .in2(regs_de_8_bits_3_out),
    .in3(regs_de_8_bits_4_out), .out(S1), .sel(R1));
  Multiplexer #(.select(2), .width(8), .enable("false")) multiplexer_2 (
    .in0(regs_de_8_bits_1_out), .in1(regs_de_8_bits_2_out), .in2(regs_de_8_bits_3_out),
    .in3(regs_de_8_bits_4_out), .out(S2), .sel(R2));
endmodule

// UC
module Uni_Cont (
  input  [2:0] Seletor,
  input  En,
  output RegWrite,
  output Beq,
  output MemWrite,
  output MemRead,
  output MemToReg,
  output Jump,
  output ULA_Src,
  output [1:0] ULA_OP
);

  wire demultiplexer_1_out0, demultiplexer_1_out1;

  or or_1 (RegWrite, demultiplexer_1_out0, MemRead, demultiplexer_1_out1);
  Demultiplexer #(.select(3), .enable("false")) demultiplexer_1 (
    .out0(demultiplexer_1_out0), .out1(demultiplexer_1_out1), .out2(Beq), .out3(MemRead), .out4(MemWrite),
    .out5(Jump), .in(En), .sel(Seletor));  // open: out6, out7
  or or_2 (ULA_Src, MemRead, MemWrite);
  Multiplexer #(.select(3), .width(2), .enable("false")) multiplexer_1 (
    .in0(2'b10), .in1(2'b11), .in2(2'b11), .in3(2'b10), .in4(2'b10), .out(ULA_OP), .sel(Seletor));  // open: in5, in6, in7

  assign MemToReg = MemRead;
endmodule

module ULA (
  input  [7:0] InA,
  input  [7:0] InB,
  input  [1:0] ULA_OP,
  output [7:0] Out,
  output Zero
);

  wire subtractor_1_bout;
  wire [7:0] adder_1_out, and_1_out, or_1_out, subtractor_1_out;

  assign and_1_out = InA & InB;  // AND_Gate and_1, 8 bits wide
  assign or_1_out = InA | InB;  // OR_Gate or_1, 8 bits wide
  Adder adder_1 (.a(InA), .b(InB), .out(adder_1_out));  // open: cin, cout
  Subtractor subtractor_1 (.a(InA), .b(InB), .out(subtractor_1_out), .bout(subtractor_1_bout));  // open: bin
  Multiplexer #(.select(2), .width(8), .enable("false")) multiplexer_1 (
    .in0(and_1_out), .in1(or_1_out), .in2(adder_1_out), .in3(subtractor_1_out), .out(Out), .sel(ULA_OP));
  nand nand_1 (Zero, Out[0], Out[1], Out[2], Out[3], Out[4], Out[5], Out[6], Out[7], subtractor_1_bout);
endmodule
